# Fritzing sketch Arduino_LM35 (saved by Fritzing 0.9.3b)
breadboards: 1

parts:
  Part1 = Arduino Uno (Rev3)
  T1 = LM35 Temperature Sensor [package="TO92 [THT]"]

nets:
  N1: Part1.A1, T1.Vout
  N2: Part1.5V, T1.+Vs
